// Logisim project processor.circ as structural Verilog: 14 circuits, main circuit rf4
module main (
  input  [31:0] DataIn,
  input  reset,
  input  clk,
  input  [1:0] selA,
  input  [1:0] selB,
  input  writeEnable,
  input  [1:0] writeReg,
  output [31:0] outA,
  output [31:0] outB
);

  wire decoder_1_out0, decoder_1_out1, decoder_1_out2, decoder_1_out3;
  wire [31:0] register_1_q, register_2_q, register_3_q, register_4_q;

  Decoder #(.select(2)) decoder_1 (
    .out0(decoder_1_out0), .out1(decoder_1_out1), .out2(decoder_1_out2), .out3(decoder_1_out3),
    .sel(writeReg), .en(writeEnable));
  Register #(.width(32)) register_1 (.D(DataIn), .en(decoder_1_out0), .clk(clk), .Q(register_1_q), .clr(reset));
  Register #(.width(32)) register_2 (.D(DataIn), .en(decoder_1_out1), .clk(clk), .Q(register_2_q), .clr(reset));
  Register #(.width(32)) register_3 (.D(DataIn), .en(decoder_1_out2), .clk(clk), .Q(register_3_q), .clr(reset));
  Register #(.width(32)) register_4 (.D(DataIn), .en(decoder_1_out3), .clk(clk), .Q(register_4_q), .clr(reset));
  Multiplexer #(.select(2), .width(32), .enable("false")) multiplexer_1 (
    .in0(register_1_q), .in1(register_2_q), .in2(register_3_q), .in3(register_4_q), .out(outA), .sel(selA));
  Multiplexer #(.select(2), .width(32), .enable("false")) multiplexer_2 (
    .in0(register_1_q), .in1(register_2_q), .in2(register_3_q), .in3(register_4_q), .out(outB), .sel(selB));
endmodule

module rf4 (
  input  writeEnable,
  input  [4:0] writeReg,
  input  [4:0] rdA,
  input  [4:0] rdB,
  input  [31:0] DataIn,
  input  reset,
  input  clk,
  output [31:0] outA,
  output [31:0] outB
);

  wire decoder_1_out0, decoder_1_out1, decoder_1_out2, decoder_1_out3, decoder_1_out4, decoder_1_out5,
       decoder_1_out6, decoder_1_out7, fwdA, fwdB;
  wire [31:0] main_1_outa, main_1_outb, main_2_outa, main_2_outb, main_3_outa, main_3_outb, main_4_outa,
       main_4_outb, main_5_outa, main_5_outb, main_6_outa, main_6_outb, main_7_outa, main_7_outb,
       multiplexer_1_out, multiplexer_2_out, reg04_1_outa, reg04_1_outb;

  Decoder #(.select(3)) decoder_1 (
    .out0(decoder_1_out0), .out1(decoder_1_out1), .out2(decoder_1_out2), .out3(decoder_1_out3),
    .out4(decoder_1_out4), .out5(decoder_1_out5), .out6(decoder_1_out6), .out7(decoder_1_out7),
    .sel(writeReg[4:2]), .en(writeEnable));
  comp comp_1 (.wrReg(writeReg), .rdReg(rdA), .forward(fwdA));
  comp comp_2 (.wrReg(writeReg), .rdReg(rdB), .forward(fwdB));
  reg04 reg04_1 (
    .DataIn(DataIn), .reset(reset), .clk(clk), .selA(rdA[1:0]), .selB(rdB[1:0]),
    .writeEnable(decoder_1_out0), .writeReg(writeReg[1:0]), .OutA(reg04_1_outa), .OutB(reg04_1_outb));
  main main_1 (
    .DataIn(DataIn), .reset(reset), .clk(clk), .selA(rdA[1:0]), .selB(rdB[1:0]),
    .writeEnable(decoder_1_out1), .writeReg(writeReg[1:0]), .outA(main_1_outa), .outB(main_1_outb));
  main main_2 (
    .DataIn(DataIn), .reset(reset), .clk(clk), .selA(rdA[1:0]), .selB(rdB[1:0]),
    .writeEnable(decoder_1_out2), .writeReg(writeReg[1:0]), .outA(main_2_outa), .outB(main_2_outb));
  main main_3 (
    .DataIn(DataIn), .reset(reset), .clk(clk), .selA(rdA[1:0]), .selB(rdB[1:0]),
    .writeEnable(decoder_1_out3), .writeReg(writeReg[1:0]), .outA(main_3_outa), .outB(main_3_outb));
  main main_4 (
    .DataIn(DataIn), .reset(reset), .clk(clk), .selA(rdA[1:0]), .selB(rdB[1:0]),
    .writeEnable(decoder_1_out4), .writeReg(writeReg[1:0]), .outA(main_4_outa), .outB(main_4_outb));
  main main_5 (
    .DataIn(DataIn), .reset(reset), .clk(clk), .selA(rdA[1:0]), .selB(rdB[1:0]),
    .writeEnable(decoder_1_out5), .writeReg(writeReg[1:0]), .outA(main_5_outa), .outB(main_5_outb));
  main main_6 (
    .DataIn(DataIn), .reset(reset), .clk(clk), .selA(rdA[1:0]), .selB(rdB[1:0]),
    .writeEnable(decoder_1_out6), .writeReg(writeReg[1:0]), .outA(main_6_outa), .outB(main_6_outb));
  main main_7 (
    .DataIn(DataIn), .reset(reset), .clk(clk), .selA(rdA[1:0]), .selB(rdB[1:0]),
    .writeEnable(decoder_1_out7), .writeReg(writeReg[1:0]), .outA(main_7_outa), .outB(main_7_outb));
  Multiplexer #(.select(3), .width(32), .enable("false")) multiplexer_1 (
    .in0(reg04_1_outa), .in1(main_1_outa), .in2(main_2_outa), .in3(main_3_outa), .in4(main_4_outa),
    .in5(main_5_outa), .in6(main_6_outa), .in7(main_7_outa), .out(multiplexer_1_out), .sel(rdA[4:2]));
  Multiplexer #(.select(3), .width(32), .enable("false")) multiplexer_2 (
    .in0(reg04_1_outb), .in1(main_1_outb), .in2(main_2_outb), .in3(main_3_outb), .in4(main_4_outb),
    .in5(main_5_outb), .in6(main_6_outb), .in7(main_7_outb), .out(multiplexer_2_out), .sel(rdB[4:2]));
  Multiplexer #(.width(32), .enable("false")) multiplexer_3 (
    .in0(multiplexer_1_out), .in1(DataIn), .out(outA), .sel(fwdA));
  Multiplexer #(.width(32), .enable("false")) multiplexer_4 (
    .in0(multiplexer_2_out), .in1(DataIn), .out(outB), .sel(fwdB));

  // Other names for the same wires on the sheet: rdAhigh[2:0] = rdA[4:2]; rdBhigh[2:0] = rdB[4:2]
endmodule

module reg04 (
  input  [31:0] DataIn,
  input  reset,
  input  clk,
  input  [1:0] selA,
  input  [1:0] selB,
  input  writeEnable,
  input  [1:0] writeReg,
  output [31:0] OutA,
  output [31:0] OutB
);

  wire decoder_1_out1, decoder_1_out2, decoder_1_out3;
  wire [31:0] register_1_q, register_2_q, register_3_q;

  Decoder #(.select(2)) decoder_1 (
    .out1(decoder_1_out1), .out2(decoder_1_out2), .out3(decoder_1_out3), .sel(writeReg), .en(writeEnable));  // open: out0
  Register #(.width(32)) register_1 (.D(DataIn), .en(decoder_1_out1), .clk(clk), .Q(register_1_q), .clr(reset));
  Register #(.width(32)) register_2 (.D(DataIn), .en(decoder_1_out2), .clk(clk), .Q(register_2_q), .clr(reset));
  Register #(.width(32)) register_3 (.D(DataIn), .en(decoder_1_out3), .clk(clk), .Q(register_3_q), .clr(reset));
  Multiplexer #(.select(2), .width(32), .enable("false")) multiplexer_1 (
    .in0({32{1'b0}}), .in1(register_1_q), .in2(register_2_q), .in3(register_3_q), .out(OutA), .sel(selA));
  Multiplexer #(.select(2), .width(32), .enable("false")) multiplexer_2 (
    .in0({32{1'b0}}), .in1(register_1_q), .in2(register_2_q), .in3(register_3_q), .out(OutB), .sel(selB));
endmodule

module comp (
  input  [4:0] wrReg,
  input  [4:0] rdReg,
  output forward
);

  wire or_1_out, xor_1_out, xor_2_out, xor_3_out, xor_4_out, xor_5_out;

  xor xor_1 (xor_1_out, wrReg[0], rdReg[0]);
  xor xor_2 (xor_2_out, wrReg[1], rdReg[1]);
  xor xor_3 (xor_3_out, wrReg[2], rdReg[2]);
  xor xor_4 (xor_4_out, wrReg[3], rdReg[3]);
  xor xor_5 (xor_5_out, wrReg[4], rdReg[4]);
  or or_1 (or_1_out, rdReg[0], rdReg[1], rdReg[2], rdReg[3], rdReg[4]);
  and and_1 (forward, xor_1_out, xor_2_out, xor_3_out, xor_4_out, xor_5_out, or_1_out);
endmodule

module IFstage (
  input  clk,
  input  [31:0] pcTarget,
  input  flowchange,
  input  flush,
  input  in_5,
  input  reset,
  output [31:0] out_7,
  output [31:0] out_8
);

  wire not_1_out;
  wire [31:0] instrMem_p3, multiplexer_1_out, PC_q;

  Register #(.width(32)) PC (.D(multiplexer_1_out), .en(not_1_out), .clk(clk), .Q(PC_q), .clr(reset));
  not not_1 (not_1_out, in_5);
  Multiplexer #(.width(32), .enable("false")) multiplexer_1 (
    .in0(out_7), .in1(pcTarget), .out(multiplexer_1_out), .sel(flowchange));
  Adder #(.width(32)) adder_1 (.a(32'h4), .b(PC_q), .out(out_7));  // open: cin, cout
  // VHDL_Entity #(.content("library ieee;\nuse ieee.std_logic_1164.all;\nuse ieee.std_logic_textio.all;\nuse ieee.numeric_std.all;\nuse std.textio.all;\n\nentity imem is\n	port(\n		a  : in  std_logic_vector(31 downto 0);\n		rd : out std_logic_vector(31 downto 0)\n	);\nend imem;\n\narchitecture RTL of imem is\n	type memoryArray is array (127 downto 0) of std_logic_vector(31 downto 0);\n	impure function init_rom return memoryArray is\n		file inputText     : text;\n		variable inputLine : line;\n		variable temporal  : std_logic_vector(31 downto 0);\n		variable rom       : memoryArray := (others => (others => '0'));\n	begin\n		file_open(inputText, \"C:/Users/Tasos/Desktop/diplomatiki/instr_memfile.dat\", read_mode);\n		for index in 0 to 127 loop\n			if (endfile(inputText)) then\n				exit;\n			else\n				readline(inputText, inputLine);\n				hread(inputLine, temporal);\n				rom(index) := temporal;\n			end if;\n		end loop;\n		file_close(inputText);\n		return rom;\n	end init_rom;\n	signal rom : memoryArray := init_rom;\nbegin\n	rd <= rom(to_integer(unsigned(a(8 downto 2)))) after 50 ns;\nend RTL;")) instrMem: pin names not known; wires that end beside it: not_1_out, PC_q, instrMem_p3
  Multiplexer #(.width(32), .enable("false")) multiplexer_2 (
    .in0(instrMem_p3), .in1({32{1'b0}}), .out(out_8), .sel(flush));
endmodule

module IFIDpipe (
  input  in_1,
  input  [31:0] in_2,
  input  [31:0] in_3,
  input  in_4,
  input  in_5,
  output [31:0] out_6,
  output [31:0] out_7
);

  Register #(.width(32)) pcSeq (.D(in_2), .en(in_4), .clk(in_1), .Q(out_6), .clr(in_5));
  Register #(.width(32)) instr (.D(in_3), .en(in_4), .clk(in_1), .Q(out_7), .clr(in_5));
endmodule

module IDstage (
  input  clk,
  input  [31:0] pcSeq,
  input  [31:0] id_instr,
  input  [31:0] mem_aluOut,
  input  [4:0] ex_rd,
  input  ex_regWrite,
  input  ex_isLoad,
  input  [4:0] mem_rd,
  input  wb_regWrite,
  input  mem_regWr,
  input  [4:0] wb_rd,
  input  mem_isLoad,
  input  [31:0] wb_writeData,
  output [31:0] pcTarget,
  output [31:0] id_rdA,
  output [31:0] id_rdB,
  output [31:0] id_imm,
  output [2:0] id_alucont,
  output id_aluSrc,
  output [1:0] id_forwardA,
  output [1:0] id_forwardB,
  output id_isLoad,
  output id_ldstBypass,
  output id_memWrite,
  output id_memtoReg,
  output [4:0] id_rd,
  output id_regWrite,
  output flush,
  output flowChange,
  output stall
);

  wire comparator_1_eq, mainDecoder_p3, mainDecoder_p4, mainDecoder_p5, mainDecoder_p7, mainDecoder_p8,
       mainDecoder_p9, mainDecoder_p11, mainDecoder_p12, mainDecoder_p14, not_1_out, pipelineControl_p7,
       pipelineControl_p19, pipelineControl_p20;
  wire [27:0] bit_extender_1_out, shifter_1_out;
  wire [31:0] adder_1_out, bit_extender_2_out, bit_extender_3_out, multiplexer_4_out, multiplexer_5_out,
       shifter_2_out;

  assign bit_extender_1_out = {{2{1'b0}}, id_instr[25:0]};  // Bit_Extender bit_extender_1
  Shifter #(.width(28)) shifter_1 (.in(bit_extender_1_out), .\dist (5'b00010), .out(shifter_1_out));
  // VHDL_Entity #(.content("library ieee;\nuse ieee.std_logic_1164.all;\nuse ieee.numeric_std.all;\n\nentity maindec is\n	port(\n		op       : in  std_logic_vector(5 downto 0); -- Op Code Field of Instruction.\n		funct    : in  std_logic_vector(5 downto 0); -- Funct Field of R-type Instructions.\n		branch   : out std_logic;\n		jump     : out std_logic;\n		lui      : out std_logic;\n		isLoad   : out std_logic;\n		isStore  : out std_logic;\n		isNop    : out std_logic; -- This is all 0s, as sll $zero, $zero, $zero.\n		readsRs  : out std_logic; -- The Instruction reads the 1st source register (rs).\n		readsRt  : out std_logic; -- The Instruction reads the 2nd source register (rt).\n		memwrite : out std_logic;\n		regwrite : out std_logic;\n		memtoreg : out std_logic;\n		regdst   : out std_logic;\n		aluctrl  : out std_logic_vector(2 downto 0);\n		alusrc   : out std_logic\n	);\nend maindec;\n\narchitecture RTL of maindec is\n	-- Implemented Instructions:\n	-- lw, sw,\n	-- beq, j,\n	-- addi, addiu (same as addi, ignores overflows),\n	-- ori,\n	-- lui,\n	-- add, sub, and, or, slt.\nbegin\n	proc : process(op, funct)\n	begin\n		-- Default Values for Signals.\n		branch   <= '0';\n		jump     <= '0';\n		lui      <= '0';\n		isLoad   <= '0';\n		isStore  <= '0';\n		isNop    <= '0';\n		readsRs  <= '1'; -- Most Instructions read the rs register.\n		readsRt  <= '0';\n		memwrite <= '0'; -- Don't write to the Data Memory.\n		regwrite <= '0'; -- Don't write result to the Register File.\n		memtoreg <= 'X'; -- Result Mux, unimportant.\n		regdst   <= '0'; -- Destination Register, unimportant, but set to 0 for simplicity.\n		aluctrl  <= \"XXX\"; -- ALU operation, unimportant.\n		alusrc   <= 'X'; -- Second ALU source, unimportant.\n		case op is\n			when \"000000\" =>            -- RTYPE --\n				regwrite <= '1'; -- All Implemented R-type instructions store result.\n				regdst   <= '1'; -- Rd is the Destination Register.\n				memtoreg <= '0'; -- AluOut to be stored to the Register File.\n				alusrc   <= '0'; -- Second ALU source is the register value.\n				readsRt  <= '1';\n				case funct is\n					when \"100000\" =>    -- ADD --\n						aluctrl <= \"010\";\n					when \"100010\" =>    -- SUB --\n						aluctrl <= \"110\";\n					when \"100100\" =>    -- AND --\n						aluctrl <= \"000\";\n					when \"100101\" =>    -- OR  --\n						aluctrl <= \"001\";\n					when \"101010\" =>    -- SLT --\n						aluctrl <= \"111\";\n					when \"000000\" =>    -- SLL --\n						isNop    <= '1'; -- Assuming NOP, even if rs, rt, and rd are not $zero.\n						regwrite <= '0';\n					when others =>    -- Unknown.\n						aluctrl <= \"XXX\";\n				end case;\n			when \"100011\" =>            --  LW   --\n				isLoad   <= '1';\n				regwrite <= '1'; -- Write Result to Register File.\n				regdst   <= '0'; -- Rt is the Destination Register.\n				memtoreg <= '1'; -- Signal Result is Mem Output.\n				alusrc   <= '1'; -- Second ALU source is Immediate.\n				aluctrl  <= \"010\";\n			when \"101011\" =>            --  SW   --\n				isStore  <= '1';\n				memwrite <= '1'; -- Write to Data Memory.\n				alusrc   <= '1'; -- Second ALU  source is Immediate.\n				aluctrl  <= \"010\";\n				readsRt  <= '1';\n			when \"000100\" =>            --  BEQ  --\n				branch  <= '1';\n				readsRt <= '1';\n			when \"001000\" | \"001001\" => -- ADDI, ADDIU --\n				regwrite <= '1'; -- Write Result to Register File.\n				regdst   <= '0'; -- Rt is the Destination Register.\n				memtoreg <= '0'; -- Signal Result is ALU Output.\n				alusrc   <= '1'; -- Second ALU source is Immediate.\n				aluctrl  <= \"010\";\n			when \"000010\" =>            --   J   --\n				jump    <= '1';\n				readsRs <= '0'; -- Does not read Rs.\n			when \"001111\" =>            --  LUI  --\n				lui      <= '1';\n				regwrite <= '1'; -- Write Result to Register File.\n				regdst   <= '0'; -- Rt is the Destination Register.\n				memtoreg <= '0'; -- Signal Result is ALU Output.\n				alusrc   <= '1'; -- Second ALU Source is Immediate.\n				readsRs  <= '0'; -- Does not read Rs.\n				aluctrl  <= \"001\";\n			when \"001101\" =>            --  ORI  --\n				regwrite <= '1'; -- Write Result to Register File.\n				regdst   <= '0'; -- Rt is the Destination Register.\n				memtoreg <= '0'; -- Signal Result is ALU Output.\n				alusrc   <= '1'; -- Second ALU Source is Immediate.\n				aluctrl  <= \"001\";\n			when others =>            -- Unknown --\n				isNop <= 'X'; -- Default values at the top cover this case.\n		end case;\n	end process proc;\nend RTL;")) mainDecoder: pin names not known; wires that end beside it: id_instr[31:26], id_instr[5:0], mainDecoder_p3, mainDecoder_p4, mainDecoder_p5, id_isLoad, mainDecoder_p7, mainDecoder_p8, mainDecoder_p9, mainDecoder_p9, mainDecoder_p11, mainDecoder_p12, id_memtoReg, mainDecoder_p14, id_alucont, id_aluSrc
  assign bit_extender_2_out = {{16{id_instr[15]}}, id_instr[15:0]};  // Bit_Extender bit_extender_2
  assign bit_extender_3_out = {{16{id_instr[15]}}, id_instr[15:0]};  // Bit_Extender bit_extender_3
  Multiplexer #(.width(5), .enable("false")) multiplexer_1 (
    .in0(id_instr[20:16]), .in1(id_instr[15:11]), .out(id_rd), .sel(mainDecoder_p14));
  Shifter #(.width(32)) shifter_2 (.in(bit_extender_2_out), .\dist (5'b00010), .out(shifter_2_out));
  Multiplexer #(.width(32), .enable("false")) multiplexer_2 (
    .in0(bit_extender_2_out), .in1(bit_extender_3_out), .out(id_imm), .sel(mainDecoder_p5));
  Adder #(.width(32)) adder_1 (.a(pcSeq), .b(shifter_2_out), .out(adder_1_out));  // open: cin, cout
  // VHDL_Entity #(.content("library ieee;\nuse ieee.std_logic_1164.all;\nuse ieee.numeric_std.all;\n\nentity pipe_ctrl is\n	port(\n		rs            : in  std_logic_vector(4 downto 0);\n		rt            : in  std_logic_vector(4 downto 0);\n		isStore       : in  std_logic;\n		isNop         : in  std_logic;\n		readsRs       : in  std_logic;\n		readsRt       : in  std_logic;\n		branch        : in  std_logic;\n		jump          : in  std_logic;\n		brTaken       : in  std_logic;\n		-- From Stage Ex  --\n		ex_rd         : in  std_logic_vector(4 downto 0);\n		ex_regWrite   : in  std_logic;\n		ex_isLoad     : in  std_logic;\n		-- From Stage Mem --\n		mem_rd        : in  std_logic_vector(4 downto 0);\n		mem_regWrite  : in  std_logic;\n		mem_isLoad    : in  std_logic;\n		--  For Stage IF  --\n		flush         : out std_logic;\n		flowChange    : out std_logic;\n		stall         : out std_logic;\n		--  For Stage ID  --\n		id_forwardA   : out std_logic_vector(1 downto 0) := \"00\"; -- Select Register from Register File.\n		id_forwardB   : out std_logic_vector(1 downto 0) := \"00\"; -- Select Register from Register File.\n		id_eqFwdA     : out std_logic := '0';\n		id_eqFwdB     : out std_logic := '0';\n		id_ldstBypass : out std_logic := '0'\n	);\nend  pipe_ctrl;\n\narchitecture RTL of pipe_ctrl is\n	signal ofStall : std_logic;\n	constant empty : std_logic_vector(4 downto 0) := (others => '0');\nbegin\n	stall         <= ofStall;\n	flush         <= (branch and brTaken and not ofStall) or jump;\n	flowChange    <= (branch and brTaken and not ofStall) or jump;\n	-- Forwarding Control for Operand A (rs):\n	-- 00 -- From Register File.\n	-- 01 -- From Stage Mem to Stage Ex.\n	-- 10 -- From Stage Wb to Stage Ex.\n	id_forwardA <= \"10\" when ((ex_regWrite = '1')	-- Valid Instruction producing Result at Stage Ex.\n						  and (ex_rd = rs)			-- Ex Target is our Rs source.\n						  and (readsRs = '1')		-- This is not a Jump Instruction, Rs is read from.\n						  and (rs /= empty)) else	-- Not reading $zero.\n				   \"01\" when ((mem_regWrite = '1')	-- Valid Instruction producing Result at Stage Mem.\n				   	      and (mem_rd = rs)			-- Mem Target is our Rs source.\n				   	      and (readsRs = '1')		-- This is not a Jump Instruction, Rs is read from.\n				   	      and (rs /= empty)) else	-- Not reading $zero.\n				   \"00\";\n	-- Forwarding Control for Operand B (rt):\n	-- It is only needed for R-type Instructions and Sw.\n	-- However, since the immediate mux is after the bypass mux,\n	-- it is unimportant when Rt is not a source. (e.g. addi, lw) \n	id_forwardB <= \"10\" when ((ex_regWrite = '1')	-- Valid Instruction producing Result at Stage Ex.\n		                  and (ex_rd = rt)			-- Ex target is our Rt source.\n		                  and (readsRt = '1')		-- This is not a Lui Instruction, Rt is read from.\n		                  and (rt /= empty)) else	-- Not reading $zero.\n				   \"01\" when ((mem_regWrite = '1')	-- Valid Instruction producing Result at Stage Mem.\n				   	      and (mem_rd = rt)			-- Mem Target is our Rt source.\n				   	      and (readsRt = '1')		-- This is not a Lui Instruction, Rt is read from.\n				   	      and (rt /= empty)) else	-- Not reading $zero.\n				   \"00\";\n	-- Forwarding Logic to Equality Comparator of Stage ID (Input A)\n	id_eqFwdA <= '1' when ((rs = mem_rd)              -- Mem Target is our Rs source.\n		               and (rs /= empty)              -- Not reading $zero.\n		               and (mem_isLoad = '0')         -- Not a Load, can't bypass with stall.\n		               and (mem_regWrite = '1')) else -- Valid Instruction producing Result at Stage Mem.\n		         '0';\n	-- Forwarding Logic to Equality Comparator of Stage ID (Input B)\n	id_eqFwdB <= '1' when ((rt = mem_rd)              -- Mem Target is our Rt source.\n		               and (rt /= empty)              -- Not reading $zero.\n		               and (mem_isLoad = '0')         -- Not a Load, can't bypass with stall.\n		               and (mem_regWrite = '1')) else -- Valid Instruction producing Result at Stage Mem.\n		         '0';\n	-- Forward just Loaded a value to a subsequent Store.\n	-- lw $t0, 0($s0)  # Load from s0 to t0.\n	-- sw $t0, 0($s1)  # Store from t0 to s1.\n	id_ldstBypass <= '1' when ((isStore = '1')     -- Store Word at Stage Id.\n		                   and (ex_isLoad = '1')   -- Load Word at Stage Ex.\n		                   and (ex_regWrite = '1') -- Valid Instruction producing Result at Stage Ex.\n		                   and (rt = ex_rd)        -- Store Word Register is the same one as the previous Load Word Register.\n		                   and (rt /= empty)) else -- Not reading $zero.\n		             '0';\n	stalling : process(rs, rt, isStore, isNop, readsRs, branch, ex_rd, ex_regWrite, ex_isLoad, mem_rd, mem_regWrite, mem_isLoad)\n	begin\n		ofStall <= '0'; -- Normally, no stalling happens.\n		-- -- Conservative Stalling. NO BYPASSING, except internally in register file.\n		-- Stalls for Data Dependence on Rs:\n--		if ((ex_regWrite = '1' and rs = ex_rd) or (mem_regWrite = '1' and rs = mem_rd)) and rs /= empty and readsRs = '1' and isNop = '0' then\n			-- Valid Instruction at Stage Ex and Reading the same Register, or\n			-- Valid Instruction at Stage Mem and Reading the same Register,\n			-- and the Register is not $zero, the Rs is actually read, and the Instruction is not Nop.\n--			ofStall <= '1';\n--		end if;\n		-- Stalls for Data Dependence on Rt:\n--		if ((ex_regWrite = '1' and rt = ex_rd) or (mem_regWrite = '1' and rt = mem_rd)) and rt /= empty and readsRt = '1' and isNop = '0' then\n			-- Valid Instruction at Stage Ex and Reading the same Register, or\n			-- Valid Instruction at Stage Mem and Reading the same Register,\n			-- and the Register is not $zero, the Rt is actually read, and the Instruction is not Nop.\n--			ofStall <= '1';\n--		end if;\n		-- Checking for Stalls from a Branch at Stage Id is for naught, as it is covered already.\n		-- If there is a dependence on an Instruction on Stage Wb, the value is forwarded\n		-- automatically inside the Register File, by writting itself on the same place.\n		-- -- Normal Stalling with Bypassing.\n		if branch = '1' and isNop = '0' then -- Branch Sources not ready. Beq too close to producer Rs or Rt.\n			if rs /= empty then -- Not reading $zero.\n				if rs = ex_rd and ex_regWrite = '1' then -- Rs comes from a previous Instruction.\n					ofStall <= '1';\n				elsif rs = mem_rd and mem_isLoad = '1' and mem_regWrite = '1' then 	-- Rs comes from two Instructions ago, which was a Load.\n					ofStall <= '1';													-- Instruction -3 is at Stage Wb, so it bypassed the new value through the Register File.\n				end if;\n			end if;\n			if rt /= empty then -- Not reading $zero.\n				if rt = ex_rd and ex_regWrite = '1' then -- Rt comes from a previous Instruction.\n					ofStall <= '1';\n				elsif rt = mem_rd and mem_isLoad = '1' and mem_regWrite = '1' then 	-- Rt comes from two Instructions ago, which was a Load.\n					ofStall <= '1';													-- Instruction -3 is at Stage Wb, so it bypassed the new value through the Register File.\n				end if;\n			end if;\n		-- Load-use Stall:\n	elsif ex_isLoad = '1' and ex_regWrite = '1' and rs = ex_rd and rs /= empty and readsRs = '1' and isNop = '0' then\n			-- Valid Load at Stage Ex, of the same Register, Rs not $zero, Rs is actually used, and it is not a Nop.\n			ofStall <= '1';\n		elsif ex_isLoad = '1' and ex_regWrite = '1' and rt = ex_rd and rt /= empty and readsRs = '1' and isNop = '0' and isStore = '0' then\n			-- Valid Load at Stage Ex, of the same Register, Rt not $zero, Rt is actually used, and it is not a Nop. Also, it is not a Store, which bypasses Rt.\n			ofStall <= '1';\n		end if;\n	end process stalling;\nend RTL;")) pipelineControl: pin names not known; wires that end beside it: id_instr[25:21], id_instr[20:16], mainDecoder_p7, mainDecoder_p8, mainDecoder_p3, mainDecoder_p4, pipelineControl_p7, ex_rd, ex_regWrite, ex_isLoad, mem_rd, mem_regWr, mem_isLoad, flush, flowChange, stall, id_forwardA, id_forwardB, pipelineControl_p19, pipelineControl_p20, id_ldstBypass
  Multiplexer #(.width(32), .enable("false")) multiplexer_3 (
    .in0(adder_1_out), .in1({pcSeq[31:28], shifter_1_out}), .out(pcTarget), .sel(mainDecoder_p4));
  rf4 rf4_1 (
    .clk(clk), .DataIn(wb_writeData), .rdB(wb_rd), .rdA(id_instr[20:16]), .writeReg(id_instr[25:21]),
    .writeEnable(wb_regWrite), .outA(id_rdA), .outB(id_rdB));  // open: reset
  Multiplexer #(.width(32), .enable("false")) multiplexer_4 (
    .in0(id_rdA), .in1(mem_aluOut), .out(multiplexer_4_out), .sel(pipelineControl_p19));
  Multiplexer #(.width(32), .enable("false")) multiplexer_5 (
    .in0(id_rdB), .in1(mem_aluOut), .out(multiplexer_5_out), .sel(pipelineControl_p20));
  Comparator #(.width(32)) comparator_1 (
    .a(multiplexer_4_out), .b(multiplexer_5_out), .eq(comparator_1_eq));  // open: gt, lt
  and and_1 (id_memWrite, mainDecoder_p11, not_1_out);
  and and_2 (id_regWrite, mainDecoder_p12, not_1_out);
  not not_1 (not_1_out, stall);
  and and_3 (pipelineControl_p7, comparator_1_eq, mainDecoder_p3);
endmodule

module IDEXpipe (
  input  in_1,
  input  [31:0] in_2,
  input  [31:0] in_3,
  input  [31:0] in_4,
  input  [2:0] in_5,
  input  in_6,
  input  [1:0] in_7,
  input  [1:0] in_8,
  input  in_9,
  input  in_10,
  input  in_11,
  input  in_12,
  input  [4:0] in_13,
  input  in_14,
  input  in_15,
  output [31:0] out_16,
  output [31:0] out_17,
  output [31:0] out_18,
  output [2:0] out_19,
  output out_20,
  output [1:0] out_21,
  output [1:0] out_22,
  output out_23,
  output out_24,
  output out_25,
  output out_26,
  output [4:0] out_27,
  output out_28
);

  Register #(.width(32)) rdA (.D(in_2), .en(1'b1), .clk(in_1), .Q(out_16), .clr(in_15));
  Register #(.width(32)) rdB (.D(in_3), .en(1'b1), .clk(in_1), .Q(out_17), .clr(in_15));
  Register #(.width(32)) imm (.D(in_4), .en(1'b1), .clk(in_1), .Q(out_18), .clr(in_15));
  Register #(.width(3)) alucont (.D(in_5), .en(1'b1), .clk(in_1), .Q(out_19), .clr(in_15));
  Register #(.width(1)) aluSrc (.D(in_6), .en(1'b1), .clk(in_1), .Q(out_20), .clr(in_15));
  Register #(.width(2)) forwardA (.D(in_7), .en(1'b1), .clk(in_1), .Q(out_21), .clr(in_15));
  Register #(.width(2)) forwardB (.D(in_8), .en(1'b1), .clk(in_1), .Q(out_22), .clr(in_15));
  Register #(.width(1)) isLoad (.D(in_9), .en(1'b1), .clk(in_1), .Q(out_23), .clr(in_15));
  Register #(.width(1)) ldstBypass (.D(in_10), .en(1'b1), .clk(in_1), .Q(out_24), .clr(in_15));
  Register #(.width(1)) memWrite (.D(in_11), .en(1'b1), .clk(in_1), .Q(out_25), .clr(in_15));
  Register #(.width(1)) memToReg (.D(in_12), .clk(in_1), .Q(out_26), .clr(in_15));  // open: en
  Register #(.width(5)) rd (.D(in_13), .en(1'b1), .clk(in_1), .Q(out_27), .clr(in_15));
  Register #(.width(1)) regWrite (.D(in_14), .en(1'b1), .clk(in_1), .Q(out_28), .clr(in_15));
endmodule

module EXstage (
  input  [31:0] ex_rdA,
  input  [31:0] ex_rdB,
  input  [31:0] ex_imm,
  input  [2:0] ex_alucont,
  input  ex_aluSrc,
  input  [1:0] ex_forwardA,
  input  [1:0] ex_forwardB,
  input  ex_isLoad,
  input  ex_ldstBypass,
  input  ex_memWrite,
  input  ex_memtoReg,
  input  [4:0] ex_rd,
  input  ex_regWrite,
  input  [31:0] wb_writeData,
  input  [31:0] mem_aluOut,
  output [31:0] ex_aluOut,
  output [31:0] ex_src2,
  output out_18,
  output out_19,
  output out_20,
  output out_21,
  output [4:0] out_22,
  output out_23
);

  wire [31:0] multiplexer_1_out, multiplexer_3_out;

  Multiplexer #(.select(2), .width(32), .enable("false")) multiplexer_1 (
    .in0(ex_rdA), .in1(wb_writeData), .in2(mem_aluOut), .out(multiplexer_1_out), .sel(ex_forwardA));  // open: in3
  Multiplexer #(.select(2), .width(32), .enable("false")) multiplexer_2 (
    .in0(ex_rdB), .in1(wb_writeData), .in2(mem_aluOut), .out(ex_src2), .sel(ex_forwardB));  // open: in3
  Multiplexer #(.width(32), .enable("false")) multiplexer_3 (
    .in0(ex_src2), .in1(ex_imm), .out(multiplexer_3_out), .sel(ex_aluSrc));
  // VHDL_Entity #(.content("library ieee;\nuse ieee.std_logic_1164.all;\nuse ieee.numeric_std.all;\n\nentity alu is\n	port(\n		a       : in  std_logic_vector(31 downto 0);\n		b       : in  std_logic_vector(31 downto 0);\n		alucont : in  std_logic_vector(2 downto 0);\n--		zero    : out std_logic;\n		result  : out std_logic_vector(31 downto 0)\n	);\nend alu;\n\narchitecture RTL of alu is\n	signal b2  : std_logic_vector(31 downto 0);\n	signal sum : std_logic_vector(31 downto 0);\n	signal slt : std_logic_vector(31 downto 0);\n--	signal res : std_logic_vector(31 downto 0);\n	constant empty : std_logic_vector(30 downto 0) := (others => '0');\n--	constant empty32 : std_logic_vector(31 downto 0) := (others => '0');\nbegin\n	b2     <= not b when (alucont(2) = '1') else b;\n	sum    <= std_logic_vector(unsigned(a) + unsigned(b2) + unsigned(alucont(2 downto 2)));\n	slt    <= empty & sum(31);\n	with alucont(1 downto 0) select result <= -- Has to become \"res\" to be read for \"zero\".\n		a and b after 50 ns when \"00\",\n		 a or b after 50 ns when \"01\",\n		    sum after 50 ns when \"10\",\n		    slt after 50 ns when \"11\",\n		    (others => 'X') when others;\n--	zero   <= '1' when (res = empty32) else '0';\n--	result <= res;\nend RTL;")) vhdl_entity_1: pin names not known; wires that end beside it: multiplexer_1_out, multiplexer_3_out, ex_alucont, ex_aluOut

  assign out_18 = ex_isLoad;
  assign out_19 = ex_ldstBypass;
  assign out_20 = ex_memWrite;
  assign out_21 = ex_memtoReg;
  assign out_22 = ex_rd;
  assign out_23 = ex_regWrite;
endmodule

module EXMEMpipe (
  input  in_1,
  input  [31:0] in_2,
  input  [31:0] in_3,
  input  in_4,
  input  in_5,
  input  in_6,
  input  in_7,
  input  [4:0] in_8,
  input  in_9,
  input  in_10,
  output [31:0] out_11,
  output [31:0] out_12,
  output out_13,
  output out_14,
  output out_15,
  output out_16,
  output [4:0] out_17,
  output out_18
);

  Register #(.width(32)) aluOut (.D(in_2), .en(1'b1), .clk(in_1), .Q(out_11), .clr(in_10));
  Register #(.width(32)) src2 (.D(in_3), .en(1'b1), .clk(in_1), .Q(out_12), .clr(in_10));
  Register #(.width(1)) isLoad (.D(in_4), .en(1'b1), .clk(in_1), .Q(out_13), .clr(in_10));
  Register #(.width(1)) ldstBypass (.D(in_5), .en(1'b1), .clk(in_1), .Q(out_14), .clr(in_10));
  Register #(.width(1)) memWrite (.D(in_6), .en(1'b1), .clk(in_1), .Q(out_15), .clr(in_10));
  Register #(.width(1)) memtoReg (.D(in_7), .en(1'b1), .clk(in_1), .Q(out_16), .clr(in_10));
  Register #(.width(5)) rd (.D(in_8), .en(1'b1), .clk(in_1), .Q(out_17), .clr(in_10));
  Register #(.width(1)) regWrite (.D(in_9), .en(1'b1), .clk(in_1), .Q(out_18), .clr(in_10));
endmodule

module MEMstage (
  input  clk,
  input  [31:0] mem_aluOut,
  input  [31:0] mem_src2,
  input  mem_isLoad,
  input  mem_ldstBypass,
  input  mem_memWrite,
  input  mem_memtoReg,
  input  [4:0] mem_rd,
  input  mem_regWrite,
  input  [31:0] wb_writeData,
  output [31:0] out_11,
  output [31:0] mem_mo,
  output out_13,
  output out_14,
  output [4:0] out_15,
  output out_16
);

  wire [31:0] multiplexer_1_out;

  Multiplexer #(.width(32), .enable("false")) multiplexer_1 (
    .in0(mem_src2), .in1(wb_writeData), .out(multiplexer_1_out), .sel(mem_ldstBypass));
  // VHDL_Entity #(.content("library ieee;\nuse ieee.std_logic_1164.all;\nuse ieee.std_logic_textio.all;\nuse ieee.numeric_std.all;\nuse std.textio.all;\n\nentity dmem is\n	port(\n		clk : in  std_logic;\n		we  : in  std_logic;\n		a   : in  std_logic_vector(31 downto 0);\n		wd  : in  std_logic_vector(31 downto 0);\n		rd  : out std_logic_vector(31 downto 0)\n	);\nend dmem;\n\narchitecture RTL of dmem is\n	type memoryArray is array (63 downto 0) of std_logic_vector(31 downto 0);\n	impure function init_ram return memoryArray is\n		file inputText     : text;\n		variable inputLine : line;\n		variable temporal  : std_logic_vector(31 downto 0);\n		variable ram       : memoryArray := (others => (others => '0'));\n	begin\n		file_open(inputText, \"C:/Users/Tasos/Desktop/diplomatiki/data_memfile.dat\", read_mode);\n		for index in 0 to 127 loop\n			if (endfile(inputText)) then\n				exit;\n			else\n				readline(inputText, inputLine);\n				hread(inputLine, temporal);\n				ram(index) := temporal;\n			end if;\n		end loop;\n		file_close(inputText);\n		return ram;\n	end init_ram;\n	signal ram : memoryArray := init_ram;\nbegin\n	proc : process(clk)\n	begin\n		if (rising_edge(clk)) then\n			if (we = '1') then\n				ram(to_integer(unsigned(a(7 downto 2)))) <= wd;\n			end if;\n		end if;\n	end process proc;\n	rd <= ram(to_integer(unsigned(a(7 downto 2)))) after 50 ns;\nend RTL;")) dataMemory: pin names not known; wires that end beside it: clk, mem_memWrite, mem_aluOut, multiplexer_1_out, mem_mo

  assign out_11 = mem_aluOut;
  assign out_13 = mem_isLoad;
  assign out_14 = mem_memtoReg;
  assign out_15 = mem_rd;
  assign out_16 = mem_regWrite;
endmodule

module MEMWBpipe (
  input  in_1,
  input  [31:0] in_2,
  input  [31:0] in_3,
  input  in_4,
  input  [4:0] in_5,
  input  in_6,
  input  in_7,
  output [31:0] out_8,
  output [31:0] out_9,
  output out_10,
  output [4:0] out_11,
  output out_12
);

  Register #(.width(32)) aluOut (.D(in_2), .en(1'b1), .clk(in_1), .Q(out_8), .clr(in_7));
  Register #(.width(32)) mo (.D(in_3), .en(1'b1), .clk(in_1), .Q(out_9), .clr(in_7));
  Register #(.width(1)) memtoReg (.D(in_4), .en(1'b1), .clk(in_1), .Q(out_10), .clr(in_7));
  Register #(.width(5)) rd (.D(in_5), .en(1'b1), .clk(in_1), .Q(out_11), .clr(in_7));
  Register #(.width(1)) regWrite (.D(in_6), .en(1'b1), .clk(in_1), .Q(out_12), .clr(in_7));
endmodule

module WBstage (
  input  [31:0] wb_aluOut,
  input  [31:0] wb_mo,
  input  wb_memtoReg,
  input  [4:0] wb_rd,
  input  wb_regWrite,
  output [31:0] wb_writeData,
  output [4:0] out_7,
  output out_8
);

  Multiplexer #(.width(32), .enable("false")) multiplexer_1 (
    .in0(wb_aluOut), .in1(wb_mo), .out(wb_writeData), .sel(wb_memtoReg));

  assign out_7 = wb_rd;
  assign out_8 = wb_regWrite;
endmodule

module MIPS (
);

  wire clock_1_out, exmempipe_1_out_13, exmempipe_1_out_14, exmempipe_1_out_15, exmempipe_1_out_16,
       exmempipe_1_out_18, exstage_1_out_18, exstage_1_out_19, exstage_1_out_20, exstage_1_out_21,
       exstage_1_out_23, idexpipe_1_out_20, idexpipe_1_out_23, idexpipe_1_out_24, idexpipe_1_out_25,
       idexpipe_1_out_26, idexpipe_1_out_28, idstage_1_flowchange, idstage_1_flush, idstage_1_id_alusrc,
       idstage_1_id_isload, idstage_1_id_ldstbypass, idstage_1_id_memtoreg, idstage_1_id_memwrite,
       idstage_1_id_regwrite, idstage_1_stall, memstage_1_out_13, memstage_1_out_14, memstage_1_out_16,
       memwbpipe_1_out_10, memwbpipe_1_out_12, por_1_out, wbstage_1_out_8;
  wire [1:0] idexpipe_1_out_21, idexpipe_1_out_22, idstage_1_id_forwarda, idstage_1_id_forwardb;
  wire [2:0] idexpipe_1_out_19, idstage_1_id_alucont;
  wire [4:0] exmempipe_1_out_17, exstage_1_out_22, idexpipe_1_out_27, idstage_1_id_rd, memstage_1_out_15,
       memwbpipe_1_out_11, wbstage_1_out_7;
  wire [31:0] exmempipe_1_out_11, exmempipe_1_out_12, exstage_1_ex_aluout, exstage_1_ex_src2,
       idexpipe_1_out_16, idexpipe_1_out_17, idexpipe_1_out_18, idstage_1_id_imm, idstage_1_id_rda,
       idstage_1_id_rdb, idstage_1_pctarget, ifidpipe_1_out_6, ifidpipe_1_out_7, ifstage_1_out_7,
       ifstage_1_out_8, memstage_1_mem_mo, memstage_1_out_11, memwbpipe_1_out_8, memwbpipe_1_out_9,
       wbstage_1_wb_writedata;

  Clock clock_1 (.out(clock_1_out));
  POR #(.PorHighDuration(1)) por_1 (.out(por_1_out));
  IFstage ifstage_1 (
    .out_8(ifstage_1_out_8), .in_5(idstage_1_stall), .pcTarget(idstage_1_pctarget), .out_7(ifstage_1_out_7),
    .clk(clock_1_out), .reset(por_1_out), .flush(idstage_1_flush), .flowchange(idstage_1_flowchange));
  IFIDpipe ifidpipe_1 (
    .in_4(idstage_1_stall), .out_7(ifidpipe_1_out_7), .out_6(ifidpipe_1_out_6), .in_1(clock_1_out),
    .in_5(por_1_out), .in_3(ifstage_1_out_8), .in_2(ifstage_1_out_7));
  IDstage idstage_1 (
    .clk(clock_1_out), .id_rdA(idstage_1_id_rda), .pcSeq(ifidpipe_1_out_6), .stall(idstage_1_stall),
    .id_isLoad(idstage_1_id_isload), .wb_regWrite(wbstage_1_out_8), .id_forwardB(idstage_1_id_forwardb),
    .id_forwardA(idstage_1_id_forwarda), .ex_regWrite(idexpipe_1_out_28), .id_rdB(idstage_1_id_rdb),
    .id_memWrite(idstage_1_id_memwrite), .flush(idstage_1_flush), .id_ldstBypass(idstage_1_id_ldstbypass),
    .id_memtoReg(idstage_1_id_memtoreg), .id_aluSrc(idstage_1_id_alusrc), .mem_rd(memstage_1_out_15),
    .id_instr(ifidpipe_1_out_7), .id_imm(idstage_1_id_imm), .ex_rd(idexpipe_1_out_27),
    .mem_isLoad(memstage_1_out_13), .id_rd(idstage_1_id_rd), .ex_isLoad(idexpipe_1_out_23),
    .pcTarget(idstage_1_pctarget), .id_regWrite(idstage_1_id_regwrite), .mem_regWr(memstage_1_out_16),
    .flowChange(idstage_1_flowchange), .mem_aluOut(exmempipe_1_out_11),
    .wb_writeData(wbstage_1_wb_writedata), .id_alucont(idstage_1_id_alucont), .wb_rd(wbstage_1_out_7));
  IDEXpipe idexpipe_1 (
    .out_21(idexpipe_1_out_21), .out_26(idexpipe_1_out_26), .in_5(idstage_1_id_alucont),
    .in_13(idstage_1_id_rd), .out_25(idexpipe_1_out_25), .out_17(idexpipe_1_out_17),
    .in_7(idstage_1_id_forwarda), .out_27(idexpipe_1_out_27), .in_2(idstage_1_id_rda),
    .out_20(idexpipe_1_out_20), .out_19(idexpipe_1_out_19), .out_24(idexpipe_1_out_24),
    .in_6(idstage_1_id_alusrc), .out_16(idexpipe_1_out_16), .in_15(por_1_out), .out_28(idexpipe_1_out_28),
    .in_10(idstage_1_id_ldstbypass), .in_12(idstage_1_id_memtoreg), .in_11(idstage_1_id_memwrite),
    .out_23(idexpipe_1_out_23), .in_1(clock_1_out), .in_8(idstage_1_id_forwardb),
    .in_14(idstage_1_id_regwrite), .out_18(idexpipe_1_out_18), .in_4(idstage_1_id_imm),
    .in_3(idstage_1_id_rdb), .out_22(idexpipe_1_out_22), .in_9(idstage_1_id_isload));
  EXstage exstage_1 (
    .ex_aluSrc(idexpipe_1_out_20), .wb_writeData(wbstage_1_wb_writedata), .ex_forwardA(idexpipe_1_out_21),
    .ex_src2(exstage_1_ex_src2), .ex_rdB(idexpipe_1_out_17), .mem_aluOut(exmempipe_1_out_11),
    .ex_forwardB(idexpipe_1_out_22), .out_18(exstage_1_out_18), .ex_imm(idexpipe_1_out_18),
    .out_20(exstage_1_out_20), .ex_alucont(idexpipe_1_out_19), .out_22(exstage_1_out_22),
    .out_23(exstage_1_out_23), .out_19(exstage_1_out_19), .ex_memWrite(idexpipe_1_out_25),
    .ex_rdA(idexpipe_1_out_16), .ex_ldstBypass(idexpipe_1_out_24), .out_21(exstage_1_out_21),
    .ex_regWrite(idexpipe_1_out_28), .ex_aluOut(exstage_1_ex_aluout), .ex_isLoad(idexpipe_1_out_23),
    .ex_memtoReg(idexpipe_1_out_26), .ex_rd(idexpipe_1_out_27));
  EXMEMpipe exmempipe_1 (
    .out_15(exmempipe_1_out_15), .in_8(exstage_1_out_22), .out_18(exmempipe_1_out_18),
    .out_13(exmempipe_1_out_13), .in_1(clock_1_out), .in_4(exstage_1_out_18), .in_10(por_1_out),
    .out_17(exmempipe_1_out_17), .out_11(exmempipe_1_out_11), .in_3(exstage_1_ex_src2),
    .in_2(exstage_1_ex_aluout), .out_12(exmempipe_1_out_12), .out_16(exmempipe_1_out_16),
    .in_9(exstage_1_out_23), .in_5(exstage_1_out_19), .out_14(exmempipe_1_out_14), .in_6(exstage_1_out_20),
    .in_7(exstage_1_out_21));
  MEMstage memstage_1 (
    .out_11(memstage_1_out_11), .mem_memtoReg(exmempipe_1_out_16), .mem_src2(exmempipe_1_out_12),
    .out_13(memstage_1_out_13), .out_15(memstage_1_out_15), .mem_isLoad(exmempipe_1_out_13),
    .mem_rd(exmempipe_1_out_17), .mem_mo(memstage_1_mem_mo), .wb_writeData(wbstage_1_wb_writedata),
    .mem_memWrite(exmempipe_1_out_15), .mem_aluOut(exmempipe_1_out_11), .out_16(memstage_1_out_16),
    .clk(clock_1_out), .mem_ldstBypass(exmempipe_1_out_14), .mem_regWrite(exmempipe_1_out_18),
    .out_14(memstage_1_out_14));
  MEMWBpipe memwbpipe_1 (
    .in_3(memstage_1_mem_mo), .in_7(por_1_out), .out_12(memwbpipe_1_out_12), .out_10(memwbpipe_1_out_10),
    .in_4(memstage_1_out_14), .out_8(memwbpipe_1_out_8), .in_6(memstage_1_out_16), .in_2(memstage_1_out_11),
    .out_11(memwbpipe_1_out_11), .in_1(clock_1_out), .in_5(memstage_1_out_15), .out_9(memwbpipe_1_out_9));
  WBstage wbstage_1 (
    .wb_rd(memwbpipe_1_out_11), .out_8(wbstage_1_out_8), .wb_memtoReg(memwbpipe_1_out_10),
    .out_7(wbstage_1_out_7), .wb_regWrite(memwbpipe_1_out_12), .wb_aluOut(memwbpipe_1_out_8),
    .wb_mo(memwbpipe_1_out_9), .wb_writeData(wbstage_1_wb_writedata));
endmodule
